// Logisim project Circuito Calculadora.circ as structural Verilog: 4 circuits, main circuit main
// q
module main (
  input  in_1,
  input  [11:0] in_2,
  input  [11:0] in_3,
  output [11:0] out_4,
  output out_5
);

  wire not_1_out, not_2_out, not_3_out;
  wire [11:0] Complemento_a_la_base_2_out_2, Complemento_a_la_base_out_2, controlled_buffer_1_out,
       controlled_buffer_2_out;

  not not_1 (not_1_out, in_1);
  assign controlled_buffer_1_out = in_1 ? in_2 : 12'bz;  // Controlled_Buffer controlled_buffer_1
  assign controlled_buffer_2_out = not_1_out ? in_3 : 12'bz;  // Controlled_Buffer controlled_buffer_2
  complemento_a_base_2__12_bits Complemento_a_la_base (.in_1(in_2), .out_2(Complemento_a_la_base_out_2));
  complemento_a_base_2__12_bits Complemento_a_la_base_2 (.in_1(in_3), .out_2(Complemento_a_la_base_2_out_2));
  not not_2 (not_2_out, in_1);
  assign controlled_buffer_1_out = not_2_out ? Complemento_a_la_base_out_2 : 12'bz;  // Controlled_Buffer controlled_buffer_3
  not not_3 (not_3_out, not_1_out);
  assign controlled_buffer_2_out = not_3_out ? Complemento_a_la_base_2_out_2 : 12'bz;  // Controlled_Buffer controlled_buffer_4
  sumador_de_12_bits Sumador_12_bits (
    .entrada_A(controlled_buffer_1_out), .entrada_B(controlled_buffer_2_out), .out_3(out_4), .Overflow(out_5));
endmodule

// CSC
module sumador_completo (
  input  a,
  input  b,
  input  c,
  output s__carreo,
  output r__resultado
);

  wire a_b_c_out, a_b_c_prime_out, a_b_prime_c_out, a_b_prime_c_prime_out, a_prime_b_c_out,
       a_prime_b_c_prime_out, a_prime_b_prime_c_out, not_1_out, not_2_out, not_3_out;

  not not_1 (not_1_out, a);
  not not_2 (not_2_out, b);
  not not_3 (not_3_out, c);
  or a_b_c_prime (a_b_c_prime_out, a, b, not_3_out);
  or a_prime_b_c (a_prime_b_c_out, not_1_out, b, c);
  or a_b_prime_c (a_b_prime_c_out, a, not_2_out, c);
  or a_b_c (a_b_c_out, a, b, c);
  or a_prime_b_c_prime (a_prime_b_c_prime_out, not_1_out, b, not_3_out);
  or a_b_prime_c_prime (a_b_prime_c_prime_out, a, not_2_out, not_3_out);
  or a_prime_b_prime_c (a_prime_b_prime_c_out, not_1_out, not_2_out, c);
  and and_1 (s__carreo, a_b_c_prime_out, a_prime_b_c_out, a_b_prime_c_out, a_b_c_out);
  and and_2 (r__resultado, a_b_c_out, a_prime_b_c_prime_out, a_b_prime_c_prime_out, a_prime_b_prime_c_out);
endmodule

module complemento_a_base_2__12_bits (
  input  [11:0] in_1,
  output [11:0] out_2
);

  wire sumador_de_12_bits_1_overflow;
  wire [11:0] not_1_out;

  not not_1 (not_1_out[0], in_1[0]);
  not not_2 (not_1_out[1], in_1[1]);
  not not_3 (not_1_out[2], in_1[2]);
  not not_4 (not_1_out[3], in_1[3]);
  not not_5 (not_1_out[4], in_1[4]);
  not not_6 (not_1_out[5], in_1[5]);
  not not_7 (not_1_out[6], in_1[6]);
  not not_8 (not_1_out[7], in_1[7]);
  not not_9 (not_1_out[8], in_1[8]);
  not not_10 (not_1_out[9], in_1[9]);
  not not_11 (not_1_out[10], in_1[10]);
  not not_12 (not_1_out[11], in_1[11]);
  sumador_de_12_bits sumador_de_12_bits_1 (
    .entrada_A(not_1_out), .entrada_B(12'h1), .out_3(out_2), .Overflow(sumador_de_12_bits_1_overflow));
  LED overflow (.in(sumador_de_12_bits_1_overflow));
endmodule

module sumador_de_12_bits (
  input  [11:0] entrada_A,
  input  [11:0] entrada_B,
  output [11:0] out_3,
  output Overflow
);

  wire sumador_completo_1_s__carreo, sumador_completo_2_s__carreo, sumador_completo_3_s__carreo,
       sumador_completo_4_s__carreo, sumador_completo_5_s__carreo, sumador_completo_6_s__carreo,
       sumador_completo_7_s__carreo, sumador_completo_8_s__carreo, sumador_completo_9_s__carreo,
       sumador_completo_10_s__carreo, sumador_completo_11_s__carreo;

  sumador_completo sumador_completo_1 (
    .a(entrada_A[0]), .b(entrada_B[0]), .c(1'b0), .s__carreo(sumador_completo_1_s__carreo),
    .r__resultado(out_3[0]));
  sumador_completo sumador_completo_2 (
    .a(entrada_A[1]), .b(entrada_B[1]), .c(sumador_completo_1_s__carreo),
    .s__carreo(sumador_completo_2_s__carreo), .r__resultado(out_3[1]));
  sumador_completo sumador_completo_3 (
    .a(entrada_A[2]), .b(entrada_B[2]), .c(sumador_completo_2_s__carreo),
    .s__carreo(sumador_completo_3_s__carreo), .r__resultado(out_3[2]));
  sumador_completo sumador_completo_4 (
    .a(entrada_A[3]), .b(entrada_B[3]), .c(sumador_completo_3_s__carreo),
    .s__carreo(sumador_completo_4_s__carreo), .r__resultado(out_3[3]));
  sumador_completo sumador_completo_5 (
    .a(entrada_A[4]), .b(entrada_B[4]), .c(sumador_completo_4_s__carreo),
    .s__carreo(sumador_completo_5_s__carreo), .r__resultado(out_3[4]));
  sumador_completo Sumador_completo_de_dos_bits ();  // open: a, b, c, s__carreo, r__resultado
  sumador_completo sumador_completo_6 (
    .a(entrada_A[5]), .b(entrada_B[5]), .c(sumador_completo_5_s__carreo),
    .s__carreo(sumador_completo_6_s__carreo), .r__resultado(out_3[5]));
  sumador_completo sumador_completo_7 (
    .a(entrada_A[6]), .b(entrada_B[6]), .c(sumador_completo_6_s__carreo),
    .s__carreo(sumador_completo_7_s__carreo), .r__resultado(out_3[6]));
  sumador_completo sumador_completo_8 (
    .a(entrada_A[7]), .b(entrada_B[7]), .c(sumador_completo_7_s__carreo),
    .s__carreo(sumador_completo_8_s__carreo), .r__resultado(out_3[7]));
  sumador_completo sumador_completo_9 (
    .a(entrada_A[8]), .b(entrada_B[8]), .c(sumador_completo_8_s__carreo),
    .s__carreo(sumador_completo_9_s__carreo), .r__resultado(out_3[8]));
  sumador_completo sumador_completo_10 (
    .a(entrada_A[9]), .b(entrada_B[9]), .c(sumador_completo_9_s__carreo),
    .s__carreo(sumador_completo_10_s__carreo), .r__resultado(out_3[9]));
  sumador_completo sumador_completo_11 (
    .a(entrada_A[10]), .b(entrada_B[10]), .c(sumador_completo_10_s__carreo),
    .s__carreo(sumador_completo_11_s__carreo), .r__resultado(out_3[10]));
  sumador_completo sumador_completo_12 (
    .a(entrada_A[11]), .b(entrada_B[11]), .c(sumador_completo_11_s__carreo), .s__carreo(Overflow),
    .r__resultado(out_3[11]));

  // Notes on the sheet:
  //   carreo 
  //   carreo 
  //   resultado
endmodule
